# Fritzing sketch 6leds (saved by Fritzing 0.8.7b)
breadboards: 1

parts:
  LED1 = LED - 5mm [color="Red (633nm)" package="5 mm [THT]"]
  LED2 = LED - 5mm [color="Red (633nm)" package="5 mm [THT]"]
  LED3 = LED - 5mm [color="Red (633nm)" package="5 mm [THT]"]
  LED4 = LED - 5mm [color="Red (633nm)" package="5 mm [THT]"]
  LED5 = LED - 5mm [color="Red (633nm)" package="5 mm [THT]"]
  LED6 = LED - 5mm [color="Red (633nm)" package="5 mm [THT]"]
  Part1 = Arduino Uno (Rev3)
  R1 = Resistor [tolerance=±5% resistance=220 package=THT]
  R2 = Resistor [tolerance=±5% resistance=220 package=THT]
  R3 = Resistor [tolerance=±5% resistance=220 package=THT]
  R4 = Resistor [tolerance=±5% resistance=220 package=THT]
  R5 = Resistor [tolerance=±5% resistance=220 package=THT]
  R6 = Resistor [tolerance=±5% resistance=220 package=THT]

nets:
  N1: LED1.cathode, LED2.cathode, LED3.cathode, LED4.cathode, LED5.cathode, LED6.cathode, Part1.GND
  N2: LED1.anode, R6.Pin_0
  N3: LED2.anode, R5.Pin_0
  N4: LED3.anode, R4.Pin_0
  N5: LED4.anode, R3.Pin_0
  N6: LED5.anode, R2.Pin_0
  N7: LED6.anode, R1.Pin_0
  N8: Part1.D2, R1.Pin_1
  N9: Part1.D3_PWM, R2.Pin_1
  N10: Part1.D4, R3.Pin_1
  N11: Part1.D5_PWM, R4.Pin_1
  N12: Part1.D6_PWM, R5.Pin_1
  N13: Part1.D7, R6.Pin_1
