# Fritzing sketch ldr (saved by Fritzing 0.8.7b)
breadboards: 1

parts:
  Part1 = Arduino Uno (Rev3)
  R1 = Photocell (LDR) [package=THT]
  R2 = Resistor [tolerance=±5% resistance=10k package=THT]
  R3 = Resistor [tolerance=±5% resistance=220 package=THT]
  LED1 = smd LED [color="Red (635nm)" package="0603 [SMD]"]

nets:
  N1: Part1.A0, R1.pin_1, R2.Pin_0
  N2: Part1.GND, R2.Pin_1, LED1.cathode
  N3: Part1.D3_PWM, R3.Pin_1
  N4: Part1.5V, R1.pin_0
  N5: R3.Pin_0, LED1.anode
