# Fritzing sketch led_switch (saved by Fritzing 0.8.7b)
breadboards: 1

parts:
  Part1 = Arduino Uno (Rev3)
  R1 = Resistor [tolerance=±5% resistance=10k package=THT]
  S1 = Pushbutton [package="[THT]"]

nets:
  N1: Part1.D2, R1.Pin_0, S1.Pin_1, S1.Pin_2
  N2: Part1.5V, R1.Pin_1
  N3: Part1.GND, S1.Pin_3, S1.Pin_4
