# Fritzing sketch stopwatch (saved by Fritzing 0.8.7b)
breadboards: 1

parts:
  R1 = Resistor [tolerance=±5% resistance=10k package=THT]
  R2 = Resistor [tolerance=±5% resistance=10k package=THT]
  S1 = Pushbutton [package="[THT]"]
  S2 = Pushbutton [package="[THT]"]
  Part1 = Arduino Uno (Rev3)

nets:
  N1: R1.Pin_0, S1.Pin_1, S1.Pin_2, Part1.D3_PWM
  N2: R1.Pin_1, R2.Pin_1, Part1.GND
  N3: R2.Pin_0, S2.Pin_1, S2.Pin_2, Part1.D2
  N4: S1.Pin_3, S1.Pin_4, S2.Pin_3, S2.Pin_4, Part1.5V
